// Logisim project SAP1.circ as structural Verilog: 10 circuits, main circuit main
module main (
  output [7:0] out_1
);

  wire Clear_out, CLK, CLK_caa0be3c, controller_1_ce_7076b96a, controller_1_clr, controller_1_clr_d8c7be46,
       controller_1_cp, controller_1_ei_8cfcdd73, controller_1_ep, controller_1_li_918300b3,
       controller_1_lm_9136fd02, dipswitch_1_sw1, Step_out;
  wire [3:0] instructionregister_1_ibus;

  DipSwitch #(.number(2)) dipswitch_1 (.sw1(dipswitch_1_sw1));  // open: sw2
  Button Clear (.out(Clear_out));
  Button Step (.out(Step_out));
  Controller controller_1 (
    .S5(Clear_out), .S6(Step_out), .S7(dipswitch_1_sw1), .Instruction(instructionregister_1_ibus),
    .CLR(controller_1_clr), .CLR_d8c7be46(controller_1_clr_d8c7be46), .CLK(CLK), .CLK_caa0be3c(CLK_caa0be3c),
    .Cp(controller_1_cp), .Ep(controller_1_ep), .Lm_9136fd02(controller_1_lm_9136fd02),
    .CE_7076b96a(controller_1_ce_7076b96a), .Li_918300b3(controller_1_li_918300b3),
    .Ei_8cfcdd73(controller_1_ei_8cfcdd73));  // open: La_56e72337, Ea, Su, Eu, Lb_84df18a1, Lo_b48aeaf1
  // Probe on out_1
  ProgramCounter programcounter_1 (
    .Ep(controller_1_ep), .Cp(controller_1_cp), .CLK_caa0be3c(CLK_caa0be3c),
    .CLR_d8c7be46(controller_1_clr_d8c7be46), .PC(out_1));
  // Probe on instructionregister_1_ibus
  MAR mar_1 (
    .WBus_in(out_1), .Lm_9136fd02(controller_1_lm_9136fd02), .CLK(CLK),
    .CE_7076b96a(controller_1_ce_7076b96a), .WBus_out(out_1));
  InstructionRegister instructionregister_1 (
    .WBus_in(out_1), .Li_918300b3(controller_1_li_918300b3), .CLK(CLK),
    .Ei_8cfcdd73(controller_1_ei_8cfcdd73), .CLR(controller_1_clr), .WBus_out(out_1),
    .IBus(instructionregister_1_ibus));

  // Notes on the sheet:
  //   Manual/Auto
endmodule

module Controller (
  input  S5,
  input  S6,
  input  S7,
  input  [3:0] Instruction,
  output CLR,
  output CLR_d8c7be46,
  output CLK,
  output CLK_caa0be3c,
  output Cp,
  output Ep,
  output Lm_9136fd02,
  output CE_7076b96a,
  output Li_918300b3,
  output Ei_8cfcdd73,
  output La_56e72337,
  output Ea,
  output Su,
  output Eu,
  output Lb_84df18a1,
  output Lo_b48aeaf1
);

  wire clock_1_out, debouncer_1_q, debouncer_2_q, debouncer_2_q_004d3fca, HLT_76c29af8, j_k_ff_1_q,
       nand_1_out, nand_2_out, nand_3_out, not_1_out, not_2_out, not_3_out, not_4_out;
  wire [5:0] State;

  // Probe on State
  RingCounter ringcounter_1 (.CLK(CLK), .CLR(CLR_d8c7be46), .out_3(State));
  not not_1 (not_1_out, S6);
  not not_2 (not_2_out, S7);
  Clock clock_1 (.out(clock_1_out));
  J_K_Flip_Flop j_k_ff_1 (
    .J(HLT_76c29af8), .K(HLT_76c29af8), .clk(clock_1_out), .Q(j_k_ff_1_q), .reset(CLR));  // open: Qn, preset
  DipSwitch #(.number(12)) dipswitch_1 (
    .sw1(Cp), .sw2(Ep), .sw3(Lm_9136fd02), .sw4(CE_7076b96a), .sw5(Li_918300b3), .sw6(Ei_8cfcdd73),
    .sw7(La_56e72337), .sw8(Ea), .sw9(Su), .sw10(Eu), .sw11(Lb_84df18a1), .sw12(Lo_b48aeaf1));
  Debouncer debouncer_1 (.S(not_1_out), .R(S6), .Q(debouncer_1_q));  // open: Q_004d3fca
  Debouncer debouncer_2 (.S(not_2_out), .R(S7), .Q_004d3fca(debouncer_2_q_004d3fca), .Q(debouncer_2_q));
  InstruccionDecoder instrucciondecoder_1 (
    .Instruction(Instruction), .HTL_86a13652(HLT_76c29af8));  // open: LDA, ADD, SUB, OUTT
  not not_3 (not_3_out, S5);
  nand nand_1 (nand_1_out, HLT_76c29af8, debouncer_1_q, debouncer_2_q_004d3fca);
  nand nand_2 (nand_2_out, debouncer_2_q, j_k_ff_1_q);
  Debouncer debouncer_3 (.S(not_3_out), .R(S5), .Q_004d3fca(CLR), .Q(CLR_d8c7be46));
  nand nand_3 (nand_3_out, nand_1_out, nand_2_out);
  not not_4 (not_4_out, nand_3_out);
  not not_5 (CLK, not_4_out);
  not not_6 (CLK_caa0be3c, nand_3_out);

  // Notes on the sheet:
  //   Single Step
  //   Manual/Auto
  //   Ring Counter
  //   Clock Circuit
  //   Clear/Start
endmodule

module RingCounter (
  input  CLK,
  input  CLR,
  output [5:0] out_3
);

  wire j_k_ff_1_q, j_k_ff_2_qn, j_k_ff_3_qn, j_k_ff_4_qn, j_k_ff_5_qn, j_k_ff_6_qn, not_1_out, not_2_out;

  not not_1 (not_1_out, CLK);
  not not_2 (not_2_out, CLR);
  J_K_Flip_Flop j_k_ff_1 (
    .J(j_k_ff_6_qn), .K(out_3[5]), .clk(not_1_out), .Q(j_k_ff_1_q), .Qn(out_3[0]), .reset(not_2_out));  // open: preset
  J_K_Flip_Flop j_k_ff_2 (
    .J(out_3[0]), .K(j_k_ff_1_q), .clk(not_1_out), .Q(out_3[1]), .Qn(j_k_ff_2_qn), .reset(not_2_out));  // open: preset
  J_K_Flip_Flop j_k_ff_3 (
    .J(out_3[1]), .K(j_k_ff_2_qn), .clk(not_1_out), .Q(out_3[2]), .Qn(j_k_ff_3_qn), .reset(not_2_out));  // open: preset
  J_K_Flip_Flop j_k_ff_4 (
    .J(out_3[2]), .K(j_k_ff_3_qn), .clk(not_1_out), .Q(out_3[3]), .Qn(j_k_ff_4_qn), .reset(not_2_out));  // open: preset
  J_K_Flip_Flop j_k_ff_5 (
    .J(out_3[3]), .K(j_k_ff_4_qn), .clk(not_1_out), .Q(out_3[4]), .Qn(j_k_ff_5_qn), .reset(not_2_out));  // open: preset
  J_K_Flip_Flop j_k_ff_6 (
    .J(out_3[4]), .K(j_k_ff_5_qn), .clk(not_1_out), .Q(out_3[5]), .Qn(j_k_ff_6_qn), .reset(not_2_out));  // open: preset
endmodule

module InstructionRegister (
  input  [7:0] WBus_in,
  input  Li_918300b3,
  input  CLK,
  input  Ei_8cfcdd73,
  input  CLR,
  output [7:0] WBus_out,
  output [3:0] IBus
);

  // Probe on WBus_in[7:4]
  // Probe on WBus_in[3:0]
  c74LS173 c74ls173_1 (
    .D(WBus_in[3:0]), .CLK_7(CLK), .G1_9_198a68ec(Li_918300b3), .G2_10_44a33287(Li_918300b3), .CLR_15(1'b0),
    .M_1(Ei_8cfcdd73), .N_2(Ei_8cfcdd73), .Q(WBus_out[3:0]));
  c74LS173 c74ls173_2 (
    .D(WBus_in[7:4]), .CLK_7(CLK), .G1_9_198a68ec(Li_918300b3), .G2_10_44a33287(Li_918300b3), .CLR_15(CLR),
    .M_1(1'b0), .N_2(1'b0), .Q(IBus));
endmodule

module ProgramCounter (
  input  Ep,
  input  Cp,
  input  CLK_caa0be3c,
  input  CLR_d8c7be46,
  output [7:0] PC
);

  wire not_1_out, not_2_out, not_3_out, not_4_out, not_5_out;
  wire [7:0] c74LS126_q;

  not not_1 (not_1_out, CLK_caa0be3c);
  not not_2 (not_2_out, CLR_d8c7be46);
  J_K_Flip_Flop c74LS126 (.J(Cp), .K(Cp), .clk(not_1_out), .Q(c74LS126_q[0]), .reset(not_2_out));  // open: Qn, preset
  not not_3 (not_3_out, c74LS126_q[0]);
  J_K_Flip_Flop j_k_ff_1 (.J(Cp), .K(Cp), .clk(not_3_out), .Q(c74LS126_q[1]), .reset(not_2_out));  // open: Qn, preset
  not not_4 (not_4_out, c74LS126_q[1]);
  J_K_Flip_Flop j_k_ff_2 (.J(Cp), .K(Cp), .clk(not_4_out), .Q(c74LS126_q[2]), .reset(not_2_out));  // open: Qn, preset
  not not_5 (not_5_out, c74LS126_q[2]);
  J_K_Flip_Flop j_k_ff_3 (.J(Cp), .K(Cp), .clk(not_5_out), .Q(c74LS126_q[3]), .reset(not_2_out));  // open: Qn, preset
  assign PC = Ep ? c74LS126_q : 8'bz;  // Controlled_Buffer controlled_buffer_1
endmodule

module MAR (
  input  [7:0] WBus_in,
  input  Lm_9136fd02,
  input  CLK,
  input  CE_7076b96a,
  output [7:0] WBus_out
);

  wire multiplexer_2_out, not_1_out, not_2_out, RUN_PROG_sw2, WRITE_sw1;
  wire [3:0] ADDRESS_sw4, c74LS173_q, controlled_buffer_1_out, multiplexer_1_out;
  wire [7:0] c74189_dout, DATA_sw8;

  not not_1 (not_1_out, Lm_9136fd02);
  // Probe on controlled_buffer_1_out
  assign controlled_buffer_1_out = not_1_out ? WBus_in[3:0] : 4'bz;  // Controlled_Buffer controlled_buffer_1
  DipSwitch #(.number(4)) ADDRESS (
    .sw1(ADDRESS_sw4[3]), .sw2(ADDRESS_sw4[2]), .sw3(ADDRESS_sw4[1]), .sw4(ADDRESS_sw4[0]));
  // Probe on c74LS173_q
  Register #(.width(4)) c74LS173 (.D(controlled_buffer_1_out), .en(not_1_out), .clk(CLK), .Q(c74LS173_q), .clr(1'b0));
  // Probe on multiplexer_1_out
  DipSwitch #(.number(2)) RUN_PROG (.sw2(RUN_PROG_sw2));  // open: sw1
  DipSwitch #(.number(2)) WRITE (.sw1(WRITE_sw1));  // open: sw2
  Multiplexer #(.width(4), .enable("false")) multiplexer_1 (
    .in0(ADDRESS_sw4), .in1(c74LS173_q), .out(multiplexer_1_out), .sel(RUN_PROG_sw2));
  Multiplexer #(.enable("false")) multiplexer_2 (
    .in0(1'b0), .in1(CE_7076b96a), .out(multiplexer_2_out), .sel(RUN_PROG_sw2));
  not not_2 (not_2_out, multiplexer_2_out);
  DipSwitch DATA (
    .sw1(DATA_sw8[7]), .sw2(DATA_sw8[6]), .sw3(DATA_sw8[5]), .sw4(DATA_sw8[4]), .sw5(DATA_sw8[3]),
    .sw6(DATA_sw8[2]), .sw7(DATA_sw8[1]), .sw8(DATA_sw8[0]));
  RAM #(.addrWidth(4), .databus("bibus")) c74189 (
    .addr(multiplexer_1_out), .we(WRITE_sw1), .oe(not_2_out), .clk(CLK), .din(DATA_sw8), .dout(c74189_dout));
  assign WBus_out = not_2_out ? c74189_dout : 8'bz;  // Controlled_Buffer controlled_buffer_2
  // Probe on c74189_dout

  // Notes on the sheet:
  //   c74LS157
endmodule

module c74LS173 (
  input  [3:0] D,
  input  CLK_7,
  input  G1_9_198a68ec,
  input  G2_10_44a33287,
  input  CLR_15,
  input  M_1,
  input  N_2,
  output [3:0] Q
);

  wire nor_1_out, nor_2_out;
  wire [3:0] controlled_buffer_1_out, register_1_q;

  // Probe on controlled_buffer_1_out
  assign controlled_buffer_1_out = nor_1_out ? D : 4'bz;  // Controlled_Buffer controlled_buffer_1
  nor nor_1 (nor_1_out, G1_9_198a68ec, G2_10_44a33287);
  Register #(.width(4)) register_1 (
    .D(controlled_buffer_1_out), .en(nor_1_out), .clk(CLK_7), .Q(register_1_q), .clr(CLR_15));
  // Probe on register_1_q
  nor nor_2 (nor_2_out, M_1, N_2);
  assign Q = nor_2_out ? register_1_q : 4'bz;  // Controlled_Buffer controlled_buffer_2
endmodule

module Debouncer (
  input  S,
  input  R,
  output Q_004d3fca,
  output Q
);

  nand nand_1 (Q_004d3fca, S, Q);
  nand nand_2 (Q, Q_004d3fca, R);
endmodule

module InstruccionDecoder (
  input  [3:0] Instruction,
  output LDA,
  output ADD,
  output SUB,
  output OUTT,
  output HTL_86a13652
);

  wire [3:0] not_1_out;

  assign not_1_out = ~Instruction;  // NOT_Gate not_1, 4 bits wide
  and and_1 (LDA, not_1_out[0], not_1_out[1], not_1_out[2], not_1_out[3]);
  and and_2 (ADD, Instruction[0], not_1_out[1], not_1_out[2], not_1_out[3]);
  and and_3 (SUB, not_1_out[0], Instruction[1], not_1_out[2], not_1_out[3]);
  and and_4 (OUTT, Instruction[0], Instruction[1], not_1_out[2], not_1_out[3]);
  nand nand_1 (HTL_86a13652, Instruction[0], Instruction[3]);
endmodule

module ControlMatrix (
  input  T1,
  input  T2,
  input  T3,
  input  T4,
  input  LDA,
  input  T5,
  input  ADD,
  input  SUB,
  input  iOUT,
  input  in_10,
  output Cp,
  output Ep,
  output Lm_,
  output CE_,
  output Li_,
  output Ei_,
  output La_,
  output Ea,
  output Su,
  output Eu,
  output Lb_,
  output Lo_
);

  wire and_1_out, and_2_out;

  and and_1 (and_1_out, T4, LDA);
  and and_2 (and_2_out, LDA, T5);
  nor nor_1 (Lm_, T1, and_1_out);
  nor nor_2 (CE_, T3, and_2_out);
  not not_1 (Li_, T3);
  not nor_3 (Ei_, and_1_out);  // NOR_Gate
  not nor_4 (La_, and_2_out);  // NOR_Gate
  // OR_Gate or_1 has open pins: out=Eu
  // NOR_Gate nor_5 has open pins: out=Lb_

  assign Cp = T2;
  assign Ep = T1;
endmodule
